// Logisim project 1st.circ as structural Verilog: 7 circuits, main circuit FA_1bit
module FA_1bit (
  input  A,
  input  B,
  input  Cin,
  output S,
  output Cout
);

  wire not_1_out, not_2_out, not_3_out, or_1_out, or_2_out, or_3_out, or_4_out, or_5_out, or_6_out, or_7_out,
       or_8_out;

  not not_1 (not_1_out, A);
  not not_2 (not_2_out, B);
  not not_3 (not_3_out, Cin);
  or or_1 (or_1_out, A, not_2_out, not_3_out);
  or or_2 (or_2_out, not_1_out, B, not_3_out);
  or or_3 (or_3_out, not_1_out, not_2_out, Cin);
  or or_4 (or_4_out, Cin, B, A);
  or or_5 (or_5_out, A, B, not_3_out);
  or or_6 (or_6_out, A, not_2_out, Cin);
  or or_7 (or_7_out, not_1_out, B, Cin);
  or or_8 (or_8_out, Cin, B, A);
  and and_1 (S, or_1_out, or_2_out, or_3_out, or_4_out);
  and and_2 (Cout, or_5_out, or_6_out, or_7_out, or_8_out);
endmodule

module Adder_8bit (
  input  C0,
  input  A0,
  input  B0,
  input  A1,
  input  B1,
  input  A2,
  input  B2,
  input  A3,
  input  B3,
  input  A4,
  input  B4,
  input  A5,
  input  B5,
  input  A6,
  input  B6,
  input  A7,
  input  B7,
  output S0,
  output S1,
  output S2,
  output S3,
  output S4,
  output S5,
  output S6,
  output S7,
  output Cout
);

  wire FA0_cout, FA1_cout, FA2_cout, FA3_cout, FA4_cout, FA5_cout, FA6_cout;

  FA_1bit FA0 (.A(A0), .B(B0), .Cin(C0), .S(S0), .Cout(FA0_cout));
  FA_1bit FA1 (.A(A1), .B(B1), .Cin(FA0_cout), .S(S1), .Cout(FA1_cout));
  FA_1bit FA2 (.A(A2), .B(B2), .Cin(FA1_cout), .S(S2), .Cout(FA2_cout));
  FA_1bit FA3 (.A(A3), .B(B3), .Cin(FA2_cout), .S(S3), .Cout(FA3_cout));
  FA_1bit FA4 (.A(A4), .B(B4), .Cin(FA3_cout), .S(S4), .Cout(FA4_cout));
  FA_1bit FA5 (.A(A5), .B(B5), .Cin(FA4_cout), .S(S5), .Cout(FA5_cout));
  FA_1bit FA6 (.A(A6), .B(B6), .Cin(FA5_cout), .S(S6), .Cout(FA6_cout));
  FA_1bit FA7 (.A(A7), .B(B7), .Cin(FA6_cout), .S(S7), .Cout(Cout));
endmodule

module DEC_GRAYP2_TO_BIN (
  input  X0,
  input  X1,
  input  X2,
  input  X3,
  output Y0,
  output Y1,
  output Y2,
  output Y3
);

  wire and_1_out, and_2_out, and_3_out, and_4_out, and_5_out, and_6_out, and_7_out, not_1_out, not_2_out,
       not_3_out, not_4_out;

  not not_1 (not_1_out, X0);
  not not_2 (not_2_out, X1);
  not not_3 (not_3_out, X2);
  not not_4 (not_4_out, X3);
  and and_1 (and_1_out, not_1_out, X1, X2, X3);
  and and_2 (and_2_out, X0, not_2_out, X2, X3);
  and and_3 (and_3_out, not_1_out, not_2_out, X2, not_4_out);
  and and_4 (and_4_out, X0, X1, X2, not_4_out);
  and and_5 (and_5_out, not_1_out, X1, not_3_out, not_4_out);
  and and_6 (and_6_out, not_2_out, X2, X3);
  and and_7 (and_7_out, X1, X2, not_4_out);
  and and_8 (Y2, not_2_out, X2);
  and and_9 (Y3, X1, X2, X3);
  or or_1 (Y1, and_6_out, and_7_out);
  or or_2 (Y0, and_1_out, and_2_out, and_3_out, and_4_out, and_5_out);
endmodule

module Adder_4bit (
  input  C0,
  input  A0,
  input  A1,
  input  A2,
  input  A3,
  input  B0,
  input  B1,
  input  B2,
  input  B3,
  output S0,
  output S1,
  output S2,
  output S3,
  output S4
);

  wire FA0_cout, FA1_cout, FA2_cout;

  FA_1bit FA0 (.A(A0), .B(B0), .Cin(C0), .S(S0), .Cout(FA0_cout));
  FA_1bit FA1 (.A(A1), .B(B1), .Cin(FA0_cout), .S(S1), .Cout(FA1_cout));
  FA_1bit FA2 (.A(A2), .B(B2), .Cin(FA1_cout), .S(S2), .Cout(FA2_cout));
  FA_1bit FA3 (.A(A3), .B(B3), .Cin(FA2_cout), .S(S3), .Cout(S4));
endmodule

module ENC_BIN_TO_GRAYP2 (
  input  S0,
  input  S1,
  input  S2,
  input  S3,
  input  S4,
  output OV,
  output T0,
  output T1,
  output T2,
  output T3,
  output U0,
  output U1,
  output U2,
  output U3
);

  wire and_1_out, and_2_out, and_3_out, and_4_out, and_5_out, and_6_out, and_7_out, and_8_out, and_9_out,
       and_10_out, and_11_out, and_12_out, and_13_out, and_14_out, and_15_out, and_16_out, not_1_out,
       not_2_out, not_3_out, not_4_out, not_5_out;

  not not_1 (not_1_out, S0);
  not not_2 (not_2_out, S1);
  not not_3 (not_3_out, S2);
  not not_4 (not_4_out, S3);
  not not_5 (not_5_out, S4);
  and and_1 (and_1_out, S1, S3);
  and and_2 (and_2_out, S2, S3);
  and and_3 (and_3_out, S0, S4);
  and and_4 (and_4_out, S1, S4);
  and and_5 (and_5_out, S0, S1, not_4_out);
  and and_6 (and_6_out, S1, S3, not_1_out);
  and and_7 (and_7_out, S0, S2, S3, not_2_out);
  and and_8 (and_8_out, not_1_out, not_2_out, not_3_out, not_5_out);
  and and_9 (and_9_out, not_1_out, not_2_out, not_4_out, not_5_out);
  and and_10 (and_10_out, S1, not_3_out);
  and and_11 (and_11_out, S3, not_2_out);
  and and_12 (and_12_out, not_3_out, not_5_out);
  and and_13 (and_13_out, S1, not_4_out);
  and and_14 (and_14_out, S3, not_2_out);
  and and_15 (and_15_out, S1, S2, not_4_out);
  and and_16 (and_16_out, S3, not_2_out, not_3_out);
  or or_1 (OV, and_1_out, and_2_out, S4);
  or or_2 (U0, and_3_out, and_4_out, and_5_out, and_6_out, and_7_out, and_8_out, and_9_out);
  or or_3 (U1, and_10_out, and_11_out, and_12_out);
  or or_4 (U2, and_13_out, and_14_out, S2, S4);
  or or_5 (U3, and_15_out, and_16_out, S4);
  not not_6 (T0, OV);

  assign T1 = 1'b1;
  assign T2 = 1'b0;
  assign T3 = 1'b0;
endmodule

module GRAYP2_MAIN_ADDER (
  input  A0,
  input  A1,
  input  A2,
  input  A3,
  input  B0,
  input  B1,
  input  B2,
  input  B3,
  output OV,
  output T0,
  output T1,
  output T2,
  output T3,
  output U0,
  output U1,
  output U2,
  output U3
);

  wire adder_4bit_1_s0, adder_4bit_1_s1, adder_4bit_1_s2, adder_4bit_1_s3, adder_4bit_1_s4,
       dec_grayp2_to_bin_1_y0, dec_grayp2_to_bin_1_y1, dec_grayp2_to_bin_1_y2, dec_grayp2_to_bin_1_y3,
       dec_grayp2_to_bin_2_y0, dec_grayp2_to_bin_2_y1, dec_grayp2_to_bin_2_y2, dec_grayp2_to_bin_2_y3;

  DEC_GRAYP2_TO_BIN dec_grayp2_to_bin_1 (
    .X0(A0), .X1(A1), .X2(A2), .X3(A3), .Y0(dec_grayp2_to_bin_1_y0), .Y1(dec_grayp2_to_bin_1_y1),
    .Y2(dec_grayp2_to_bin_1_y2), .Y3(dec_grayp2_to_bin_1_y3));
  DEC_GRAYP2_TO_BIN dec_grayp2_to_bin_2 (
    .X0(B0), .X1(B1), .X2(B2), .X3(B3), .Y0(dec_grayp2_to_bin_2_y0), .Y1(dec_grayp2_to_bin_2_y1),
    .Y2(dec_grayp2_to_bin_2_y2), .Y3(dec_grayp2_to_bin_2_y3));
  Adder_4bit adder_4bit_1 (
    .C0(1'b0), .A0(dec_grayp2_to_bin_1_y0), .A1(dec_grayp2_to_bin_1_y1), .A2(dec_grayp2_to_bin_1_y2),
    .A3(dec_grayp2_to_bin_1_y3), .B0(dec_grayp2_to_bin_2_y0), .B1(dec_grayp2_to_bin_2_y1),
    .B2(dec_grayp2_to_bin_2_y2), .B3(dec_grayp2_to_bin_2_y3), .S0(adder_4bit_1_s0), .S1(adder_4bit_1_s1),
    .S2(adder_4bit_1_s2), .S3(adder_4bit_1_s3), .S4(adder_4bit_1_s4));
  ENC_BIN_TO_GRAYP2 enc_bin_to_grayp2_1 (
    .S0(adder_4bit_1_s0), .S1(adder_4bit_1_s1), .S2(adder_4bit_1_s2), .S3(adder_4bit_1_s3),
    .S4(adder_4bit_1_s4), .OV(OV), .T0(T0), .T1(T1), .T2(T2), .T3(T3), .U0(U0), .U1(U1), .U2(U2), .U3(U3));
endmodule

module Counter_8_T (
  output Q0,
  output Q1,
  output Q2
);

  wire and_1_out, clock_1_out;

  Clock clock_1 (.out(clock_1_out));
  T_Flip_Flop FF0 (.T(1'b1), .clk(clock_1_out), .Q(Q0));  // open: Qn, reset, preset
  T_Flip_Flop FF1 (.T(Q0), .clk(clock_1_out), .Q(Q1));  // open: Qn, reset, preset
  T_Flip_Flop FF2 (.T(and_1_out), .clk(clock_1_out), .Q(Q2));  // open: Qn, reset, preset
  and and_1 (and_1_out, Q1, Q0);
endmodule
